# Fritzing sketch projectSketch (saved by Fritzing 0.9.2b)
breadboards: 1

parts:
  Part1 = Arduino Uno (Rev3)
  R1 = PHOTOCELL [package=photocell]
  LED1 = LED - 5mm [color="Red (633nm)" package="5 mm [THT]"]
  R2 = Resistor [tolerance=±5% resistance=220 package=THT]
  LD1 = LD

nets:
  N1: Part1.A0, R1.P$2, R2.Pin_0
  N2: Part1.D8, LD1.anode
  N3: Part1.D9_PWM, LED1.anode
  N4: Part1.5V, R1.P$1, LD1.cathode
  N5: Part1.GND, LED1.cathode, R2.Pin_1

custom parts:
  LD: A Generic Red Dot Laser Diode Module (~5mW)
